# Fritzing sketch human_i_arms (saved by Fritzing 0.9.3b)
breadboards: 1

parts:
  Part1 = Arduino Uno (Rev3) - ICSP
  hc-sr1 = hc-sr04
  Part2 = 16 NeoPixel Ring [part_number=1463]
  BATT2 = 4xAA Switchable Battery Pack w/Bare Wire
  J1 = Basic Servo

nets:
  N1: Part1.A0, J1.pulse
  GND: Part1.GND, hc-sr1.GND, Part2.GND, BATT2.NEG, J1.gnd
  N2: Part1.D2, hc-sr1.Trig
  N3: Part1.D3_PWM, hc-sr1.Echo
  N4: Part1.D4, Part2.IN
  VCC: Part1.3V3, hc-sr1.VCC, J1.vcc
  N5: Part2.VDD, BATT2.POS

custom parts:
  16 NeoPixel Ring: 16 ultra bright smart LED NeoPixels are arranged in a circle with 1.75" (44.5mm) outer diameter. The rings are 'chainable' - connect the output pin of one to the input pin of another. Use only one microcontroller pin to control as many as you can chain together! Each LED is addressable as the driver chip is inside the LED. Each one has ~18mA constant current drive so the color will be very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
  4xAA Switchable Battery Pack w/Bare Wire: 4xAA Switchable Battery Pack with Bare Wire connection
